// Logisim project muxrisccore.circ as structural Verilog: 1 circuit, main circuit main
module main (
);

  wire clock_1_out, clock_2_out, clock_3_out, clock_4_out, clock_5_out, clock_6_out, clock_7_out,
       clock_8_out, clock_9_out, comparator_1_eq, comparator_3_eq, comparator_4_eq, comparator_5_eq,
       comparator_6_eq, comparator_6_gt, comparator_7_eq, comparator_7_gt, comparator_8_eq, comparator_8_gt,
       counter_1_q, counter_2_q, multiplexer_3_out, not_1_out, not_2_out, not_3_out, not_4_out, or_1_out,
       or_2_out, or_3_out, or_4_out, register_3_q;
  wire [1:0] counter_3_q;
  wire [2:0] bitselector_1_out;
  wire [15:0] bitselector_2_out, bitselector_3_out, counter_4_q, multiplexer_1_out, multiplexer_2_out;
  wire [63:0] multiplexer_4_out, ram_1_dout, register_1_q, register_2_q, register_4_q;

  Register #(.trigger("falling"), .width(64)) register_1 (
    .D(ram_1_dout), .en(or_1_out), .clk(clock_1_out), .Q(register_1_q));  // open: clr
  or or_1 (or_1_out, or_2_out, comparator_1_eq);
  Comparator #(.width(64)) comparator_1 (.a({64{1'b0}}), .b(register_1_q), .eq(comparator_1_eq));  // open: gt, lt
  Clock clock_1 (.out(clock_1_out));
  BitSelector #(.group(3), .width(64)) bitselector_1 (.in(register_1_q), .out(bitselector_1_out), .sel({5{1'b0}}));
  Comparator #(.width(3)) comparator_2 (.a(bitselector_1_out), .b(3'b000));  // open: gt, eq, lt
  Comparator #(.width(3)) comparator_3 (.a(bitselector_1_out), .b(3'b001), .eq(comparator_3_eq));  // open: gt, lt
  not not_1 (not_1_out, comparator_3_eq);
  Clock clock_2 (.out(clock_2_out));
  Comparator #(.width(3)) comparator_4 (.a(bitselector_1_out), .b(3'b010), .eq(comparator_4_eq));  // open: gt, lt
  not not_2 (not_2_out, comparator_4_eq);
  Clock clock_3 (.out(clock_3_out));
  Comparator #(.width(3)) comparator_5 (.a(bitselector_1_out), .b(3'b011), .eq(comparator_5_eq));  // open: gt, lt
  not not_3 (not_3_out, comparator_5_eq);
  Clock clock_4 (.out(clock_4_out));
  Counter #(.max('h1), .ongoal("stay"), .trigger("falling"), .width(1)) counter_1 (
    .count(comparator_3_eq), .Q(counter_1_q), .clk(clock_2_out), .clr(not_1_out));  // open: load, D, carry, up
  Counter #(.max('h1), .ongoal("stay"), .trigger("falling"), .width(1)) counter_2 (
    .count(comparator_4_eq), .Q(counter_2_q), .clk(clock_3_out), .clr(not_2_out));  // open: load, D, carry, up
  Counter #(.max('h3), .ongoal("stay"), .trigger("falling"), .width(2)) counter_3 (
    .count(comparator_5_eq), .Q(counter_3_q), .clk(clock_4_out), .clr(not_3_out));  // open: load, D, carry, up
  or or_2 (or_2_out, or_3_out, or_4_out, comparator_8_gt);
  or or_3 (or_3_out, comparator_6_gt, comparator_6_eq);
  Comparator #(.mode("unsigned"), .width(1)) comparator_6 (
    .a(counter_1_q), .b(1'b1), .gt(comparator_6_gt), .eq(comparator_6_eq));  // open: lt
  or or_4 (or_4_out, comparator_7_gt, comparator_7_eq);
  Comparator #(.mode("unsigned"), .width(1)) comparator_7 (
    .a(counter_2_q), .b(1'b1), .gt(comparator_7_gt), .eq(comparator_7_eq));  // open: lt
  Comparator #(.mode("unsigned"), .width(2)) comparator_8 (
    .a(counter_3_q), .b(2'b01), .gt(comparator_8_gt), .eq(comparator_8_eq));  // open: lt
  not not_4 (not_4_out, comparator_8_gt);
  BitSelector #(.group(16), .width(64)) bitselector_2 (.in(ram_1_dout), .out(bitselector_2_out), .sel(2'b00));
  Counter #(.max('hffff), .width(16)) counter_4 (
    .load(or_3_out), .D(bitselector_2_out), .count(not_4_out), .Q(counter_4_q), .clk(clock_5_out));  // open: carry, up, clr
  Clock clock_5 (.out(clock_5_out));
  Register #(.width(64)) register_2 (
    .D(ram_1_dout), .en(comparator_8_eq), .clk(clock_6_out), .Q(register_2_q));  // open: clr
  Clock clock_6 (.out(clock_6_out));
  Register #(.width(1)) register_3 (.D(comparator_8_eq), .en(1'b1), .clk(clock_7_out), .Q(register_3_q));  // open: clr
  Clock clock_7 (.out(clock_7_out));
  Multiplexer #(.width(16)) multiplexer_1 (
    .in0(counter_4_q), .in1(bitselector_3_out), .out(multiplexer_1_out), .sel(register_3_q));
  BitSelector #(.group(16), .width(64)) bitselector_3 (.in(register_2_q), .out(bitselector_3_out), .sel(2'b00));
  Register #(.width(64)) register_4 (.D(ram_1_dout), .en(or_4_out), .clk(clock_8_out), .Q(register_4_q));  // open: clr
  Clock clock_8 (.out(clock_8_out));
  Multiplexer #(.select(3), .width(16)) multiplexer_2 (
    .in0(counter_4_q), .in1(counter_4_q), .in2(counter_4_q), .in3(multiplexer_1_out),
    .out(multiplexer_2_out), .sel(bitselector_1_out));  // open: in4, in5, in6, in7
  RAM #(.addrWidth(16), .dataWidth(64), .enables("line"), .\type ("nonvolatile")) ram_1 (
    .addr(multiplexer_2_out), .we(multiplexer_3_out), .clk(clock_9_out), .din(multiplexer_4_out),
    .dout(ram_1_dout));
  Clock clock_9 (.out(clock_9_out));
  Multiplexer #(.select(3)) multiplexer_3 (
    .in0(1'b0), .in1(1'b0), .in2(1'b0), .in3(comparator_8_gt), .out(multiplexer_3_out),
    .sel(bitselector_1_out));  // open: in4, in5, in6, in7
  Multiplexer #(.select(3), .width(64)) multiplexer_4 (
    .in0({64{1'b0}}), .in1({64{1'b0}}), .in2({64{1'b0}}), .in3(register_4_q), .out(multiplexer_4_out),
    .sel(bitselector_1_out));  // open: in4, in5, in6, in7
endmodule
